// Logisim project data_path.circ as structural Verilog: 1 circuit, main circuit main
module main (
  output [31:0] out_1,
  output [31:0] out_2,
  output [31:0] out_3,
  output [31:0] out_4,
  output [31:0] out_5,
  output [31:0] out_6,
  output [31:0] out_7,
  output [31:0] out_8,
  output [31:0] out_9,
  output [31:0] out_10,
  output [31:0] out_11,
  output [31:0] out_12,
  output [31:0] out_13,
  output [31:0] out_14,
  output [31:0] out_15,
  output [31:0] out_16,
  output [31:0] out_17,
  output [31:0] out_18,
  output [31:0] out_19,
  output [31:0] out_20,
  output [31:0] out_21,
  output [31:0] out_22,
  output [31:0] out_23,
  output [31:0] out_24,
  output [31:0] out_25,
  output [31:0] out_26,
  output [31:0] out_27,
  output [31:0] out_28,
  output [31:0] out_29,
  output [31:0] out_30,
  output [31:0] out_31,
  output [31:0] out_32,
  output [31:0] out_33,
  output out_34,
  output out_35
);

  wire clock, Extop, jalr, kill, kill_ID, LessFlagSigned, LessFlagUnsigned, mem_to_reg, Memory_Write,
       MemRead, pc_src, RegWrite, SSET, Stall, ZeroFlag;
  wire [1:0] ALUsrc;
  wire [4:0] ImmL, ImmL_ID, multiplexer_4_out, Rd_WB, Rs1_ID, Rs2_ID;
  wire [5:0] OP;
  wire [7:0] ALU_Op;
  wire [10:0] Funct, ImmU;
  wire [15:0] Imm16, Imm16_ID;
  wire [19:0] pc, PC_ID, pc_inc, pc_inc_ID;
  wire [31:0] ALU_Result, bit_extender_1_out, bit_extender_2_out, bit_extender_3_out, bit_extender_4_out,
       BusA, BusB, main_2_out_2, main_3_instruction_2, main_6_memory_output, multiplexer_1_out,
       multiplexer_2_out, multiplexer_3_out, multiplexer_5_out, Write_Data;

  // Probe on Imm16
  // pc_circut_main main_1: pin names not known; wires that end beside it: PC_ID, Stall, Imm16, Funct, ImmL_ID, BusA, clock, pc_src, jalr, pc_inc, pc
  // Probe on pc_inc
  // Probe on pc
  // Probe on ImmL
  // Probe on ImmU
  // Probe on pc
  assign bit_extender_1_out = {{16{1'b0}}, Imm16};  // Bit_Extender bit_extender_1
  assign bit_extender_2_out = {{16{Imm16[15]}}, Imm16};  // Bit_Extender bit_extender_2
  assign bit_extender_3_out = {{16{ImmU[10]}}, {ImmU, ImmL}};  // Bit_Extender bit_extender_3
  Multiplexer #(.width(32), .enable("false")) multiplexer_1 (
    .in0(bit_extender_1_out), .in1(bit_extender_2_out), .out(multiplexer_1_out), .sel(Extop));
  Clock clock_1 (.out(clock));
  Multiplexer #(.select(2), .width(32), .enable("false")) multiplexer_2 (
    .in0(BusB), .in1(multiplexer_1_out), .in2(bit_extender_3_out), .out(multiplexer_2_out), .sel(ALUsrc));  // open: in3
  instruction_mem_main main_2 (.in_1(pc), .out_2(main_2_out_2));
  // Probe on ALU_Op[5:4]
  Multiplexer #(.width(32), .enable("false")) multiplexer_3 (
    .in0(main_2_out_2), .in1({32{1'b0}}), .out(multiplexer_3_out), .sel(kill));
  ALU_Full alu_full_1 (
    .OverFlow(out_34), .AInvert(ALU_Op[7]), .CarryIn(ALU_Op[6]), .in_2(BusA), .in_4(multiplexer_2_out),
    .Operation(ALU_Op[5:4]), .BInvert(ALU_Op[6]), .select_Alu(ALU_Op[3:0]),
    .less_flag_signed(LessFlagUnsigned), .out_11(LessFlagSigned), .out_9(ALU_Result), .out_14(out_35),
    .zreo_flag(ZeroFlag));  // open: in_5
  // Probe on ALU_Result
  // Probe on OP
  IF_ID_REGISTER_main main_3 (
    .instruction(multiplexer_3_out), .PC_IF(pc), .pc_inc(pc_inc), .kill(kill), .clk(clock), .stall(Stall),
    .instruction_2(main_3_instruction_2), .PC_ID(PC_ID), .pc_inc_2(pc_inc_ID), .kill_2(kill_ID));
  // Fetch_instruction_main main_4: pin names not known; wires that end beside it: Imm16_ID, Rs1_ID, Rs2_ID, main_3_instruction_2, ImmL_ID, OP, Funct
  // Probe on ALU_Result
  MainControlUnit_main main_5 (
    .ALU_Op(ALU_Op), .mem_to_reg(mem_to_reg), .Memory_Read(MemRead), .Memory_Write(Memory_Write),
    .RegWrite(RegWrite), .in_1(Funct), .Extop(Extop), .ALUsrc(ALUsrc), .in_2(OP), .SSET(SSET), .jalr(jalr),
    .Pc_src(pc_src), .ZeroFlag(ZeroFlag), .LessFlagSigned(LessFlagSigned), .LessFlagUnsigned(LessFlagUnsigned));
  // Probe on Rs1_ID
  data_mem_main main_6 (
    .in_1(ALU_Result), .in_2(Memory_Write), .in_3(MemRead), .in_4(clock),
    .memory_output(main_6_memory_output), .in_5(BusB));
  // Probe on main_6_memory_output
  // Probe on ALU_Result
  Multiplexer #(.width(5), .enable("false")) multiplexer_4 (
    .in0(Rs1_ID), .in1(Rd_WB), .out(multiplexer_4_out), .sel(SSET));
  Multiplexer #(.width(32), .enable("false")) multiplexer_5 (
    .in0(ALU_Result), .in1(main_6_memory_output), .out(multiplexer_5_out), .sel(mem_to_reg));
  assign bit_extender_4_out = {{12{1'b0}}, pc_inc};  // Bit_Extender bit_extender_4
  Multiplexer #(.width(32), .enable("false")) multiplexer_6 (
    .in0(multiplexer_5_out), .in1(bit_extender_4_out), .out(Write_Data), .sel(jalr));
  // Probe on Write_Data
  Reg_file reg_file_1 (
    .out_7(out_1), .out_19(BusA), .out_28(BusB), .RW(Rd_WB), .Reg_Write(RegWrite), .DATA_IN(Write_Data),
    .clock(clock), .BusB(Rs2_ID), .BusA(multiplexer_4_out), .out_9(out_4), .out_11(out_9), .out_14(out_13),
    .out_15(out_17), .out_16(out_19), .out_17(out_23), .out_18(out_21), .out_20(out_27), .out_21(out_25),
    .out_22(out_31), .out_23(out_29), .out_24(out_3), .out_25(out_33), .out_26(out_7), .out_29(out_12),
    .out_27(out_5), .out_30(out_10), .out_32(out_16), .out_31(out_14), .out_34(out_20), .out_33(out_18),
    .out_37(out_28), .out_39(out_32), .out_36(out_22), .out_35(out_24), .out_38(out_26), .out_40(out_30),
    .out_8(out_2), .out_10(out_6), .out_12(out_11), .out_13(out_15));
  // Probe on BusB

  assign out_8 = out_7;

  // Other names for the same wires on the sheet: ImmU_ID[10:0] = Funct; R0[31:0] = out_1; R1[31:0] = out_2;
  //   R2[31:0] = out_4; R3[31:0] = out_6; R4[31:0] = out_9; R5[31:0] = out_11; R6[31:0] = out_13; R7[31:0] = out_15;
  //   R8[31:0] = out_17; R9[31:0] = out_19; R10[31:0] = out_21; R11[31:0] = out_23; R12[31:0] = out_25;
  //   R13[31:0] = out_27; R14[31:0] = out_29; R15[31:0] = out_31; R16[31:0] = out_33; R17[31:0] = out_3;
  //   R18[31:0] = out_5; R19[31:0] = out_7; R20[31:0] = out_10; R21[31:0] = out_12; R22[31:0] = out_14;
  //   R23[31:0] = out_16; R24[31:0] = out_18; R25[31:0] = out_20; R26[31:0] = out_22; R27[31:0] = out_24;
  //   R28[31:0] = out_26; R29[31:0] = out_28; R30[31:0] = out_30; R31[31:0] = out_32; Rd_ID[4:0] = ImmL_ID

  // Notes on the sheet:
  //   Registers
  //   IF
  //   TO used_in_Control_Signal
  //   EX
  //   MEM
  //   signal
  //   WB
  //   ID
endmodule
